# Fritzing sketch tempAndPhUnit (saved by Fritzing 0.9.3b)
breadboards: 1

parts:
  LCM1602_IIC1 = LCM1602 IIC [part_number="LCM1602 IIC" chip_label="LCM1602 IIC" package="DIP (Dual Inline) [THT]"]
  MH-ET_LIVE_ESP32_DEVKIT1 = MH-ET LIVE ESP32 DEVKIT 38 pins
  LED1 = LEDs [package=led10mm]
  U2 = TEMPERATURE-SENSOR [package=to-92]
  R1 = Resistor [tolerance=±5% resistance=220 package=THT]
  LCD1 = LCD screen
  S1 = PH meter [package=THT]

nets:
  VSS: LCM1602_IIC1.VSS, LCD1.VSS
  VDD: LCM1602_IIC1.VDD, LCD1.VDD
  N1: LCM1602_IIC1.V0, LCD1.V0
  N2: LCM1602_IIC1.RS, LCD1.RS
  N3: LCM1602_IIC1.RW, LCD1.R/W
  N4: LCM1602_IIC1.E, LCD1.E
  N5: LCM1602_IIC1.D0, LCD1.DB0
  N6: LCM1602_IIC1.D1, LCD1.DB1
  N7: LCM1602_IIC1.D2, LCD1.DB2
  N8: LCM1602_IIC1.D3, LCD1.DB3
  N9: LCM1602_IIC1.D4, LCD1.DB4
  N10: LCM1602_IIC1.D5, LCD1.DB5
  N11: LCM1602_IIC1.D6, LCD1.DB6
  N12: LCM1602_IIC1.D7, LCD1.DB7
  N13: LCM1602_IIC1.A, LCD1.LED+
  N14: LCM1602_IIC1.K, LCD1.LED-
  GND: LCM1602_IIC1.GND, MH-ET_LIVE_ESP32_DEVKIT1.GND, LED1.C, U2.GND, S1.pin3
  VCC: LCM1602_IIC1.VCC, MH-ET_LIVE_ESP32_DEVKIT1.5V, U2.VCC, R1.Pin_1, S1.pin2
  N15: LCM1602_IIC1.SDA, MH-ET_LIVE_ESP32_DEVKIT1.SD0
  N16: LCM1602_IIC1.SCL, MH-ET_LIVE_ESP32_DEVKIT1.SCK
  N17: MH-ET_LIVE_ESP32_DEVKIT1.3V3, LED1.A
  N18: MH-ET_LIVE_ESP32_DEVKIT1.IO35, S1.pin1
  N19: MH-ET_LIVE_ESP32_DEVKIT1.IO25, U2.ADJ, R1.Pin_0

custom parts:
  LCM1602 IIC: I2C-Module to use a 1602 or 2004 LCD on with the wire.h libory Serial LCD Modul
  MH-ET LIVE ESP32 DEVKIT 38 pins: http://mh.nodebb.com/topic/2/mh-et-live-esp32-devkit
